# Fritzing sketch NMEALogger (saved by Fritzing 0.6.3b)

parts:
  Part1 = GPS_LS20031
  Arduino1 = Arduino

nets:
  N1: Part1.connector7, Arduino1.3V3
  N2: Part1.connector9, Arduino1.D0RX
  N3: Part1.connector10, Arduino1.GND
